# Fritzing sketch Untitled Sketch (saved by Fritzing 0.9.4)

parts:
  U1 = ESP32-38PinWide [part_number=ESP32-38PinWide]
  M1 = fc-51 [package=THT]
  LED1 = RGB LED (com. cathode, rgb) [package="5 mm [THT]"]

nets:
  N1: U1.3.3, M1.pin3
  N2: U1.GPIO26, M1.pin1
  N3: U1.GND, M1.pin2, LED1.blue_anode
  N4: U1.GPIO18, LED1.red_anode
  N5: U1.GPIO19, LED1.common_cathode
  N6: U1.GPIO21, LED1.green_anode

custom parts:
  ESP32-38PinWide: Generic 38-Pin ESP32 with wide format (only access to one side of pins on a breadboard) based on Stephen Lilley's HiLetgo ESP-WROOM-32 ESP32 ESP-32S Development Board.

// code stored in the sketch: handwash.ino
const int IR = 26;
const int blue=18;
const int green=19;
const int red=21;

void setup() 
{
pinMode(IR,INPUT);  //IR sensor
pinMode(blue,OUTPUT); //RED
pinMode(green,OUTPUT); //GREEN
pinMode(red,OUTPUT); //BLUE
Serial.begin(9600);
  digitalWrite(blue,LOW); //RED off
  digitalWrite(green,LOW); //GREEN on by default
  digitalWrite(red,LOW); //BLUE off
}

void loop() 
{
  int a= digitalRead(IR);
  delay(100);
  if(a==0)
   { 
    digitalWrite(blue,HIGH); //RED off
    digitalWrite(green,LOW); //GREEN on by default
    digitalWrite(red,LOW); //BLUE off
            
       for(int i=0; i<20; i++)
         {
            digitalWrite(blue,HIGH);
            delay(1000);
         }  
     digitalWrite(blue,LOW);
     digitalWrite(green,HIGH);
     delay(3000);
     digitalWrite(green,LOW);
     digitalWrite(red,HIGH);
     delay(300);
     digitalWrite(red,LOW);
     delay(300);
     digitalWrite(red,HIGH);
     delay(300);
     digitalWrite(red,LOW);
  }

}
